# Fritzing sketch mini_ups (saved by Fritzing 0.9.3b)

parts:
  F1 = Resettable Fuse PTC [package=0603]
  D1 = Schottky Diode [part_number=1N5817 package="300 mil [THT]"]
  R1 = Resistor [tolerance=±5% resistance=10k package="0402 [SMD]"]
  R2 = Resistor [tolerance=±5% resistance=10k package="0402 [SMD]"]
  F2 = Resettable Fuse PTC [package=0603]
  D2 = Schottky Diode [part_number=1N5817 package="300 mil [THT]"]
  R3 = Resistor [tolerance=±5% resistance=10k package="0402 [SMD]"]
  R4 = Resistor [tolerance=±5% resistance=10k package="0402 [SMD]"]
  R5 = Temperature Sensor (Thermistor) [thermistor_type=NTC package=THT]
  R6 = Resistor [tolerance=±5% resistance=10k package="0402 [SMD]"]
  R7 = Resistor [tolerance=±5% resistance=10k package="0402 [SMD]"]
  R8 = Temperature Sensor (Thermistor) [thermistor_type=NTC package=THT]
  Componente1 = Arduino Nano (Rev3.0)
  Mod1 = KY-019 5V Relay Module [package="Breakout board"]
  OLED1 = OLED Mono 0.56 inch blue or white
  LLC1 = Logic Level Converter [package="Breakout board"]
  J5 = JST-B3B-XH-A [part_number=B3B-XH-A package=THT]

nets:
  N1: F1.2, D1.anode
  N2: D1.cathode, R1.Pin_0
  N3: R1.Pin_1, R2.Pin_0, Componente1.A1
  GND: R2.Pin_1, R4.Pin_1, R6.Pin_1, R7.Pin_1, Componente1.GND, Mod1.-, OLED1.GND, LLC1.H-GND
  N4: F2.1, Mod1.Common
  N5: F2.2, D2.anode
  N6: D2.cathode, R3.Pin_0
  N7: R3.Pin_1, R4.Pin_0, Componente1.A0
  N8: R5.pin_1, R6.Pin_0
  N9: R7.Pin_0, R8.pin_1
  N10: Componente1.D7, Mod1.S
  N11: Componente1.D8, LLC1.HV3
  N12: Componente1.D9, LLC1.HV
  N13: Componente1.5V, Mod1.+
  N14: Componente1.A5, OLED1.SCL
  N15: Componente1.A4, OLED1.SDA
  N16: LLC1.LV, J5.pin1
  N17: LLC1.L-GND, J5.pin2
  N18: LLC1.LV3, J5.pin3

notes:
  Protection Stage
  Source
  Protection stage
  Batteries
  between batteries
  to source +5v
  to serial Endpoint

custom parts:
  KY-019 5V Relay Module: KY-019 5V Relay module, used to control AC circuits. (Special thanks to vanepp for fixing the PCB holes and other errors)
  OLED Mono 0.56 inch blue or white: OLED, I2C 3.3V - 5V Blue and White text versions
  Logic Level Converter: 5V to/from 3.3V logic level converter
